// Logisim project And.circ as structural Verilog
module main (
  input  in_1,
  input  in_2,
  output out_3
);

  D_Flip_Flop d_ff_1 (.D(in_1), .Clock(in_2), .out_3(out_3));  // open: out_4
endmodule

module D_Flip_Flop (
  input  D,
  input  Clock,
  output out_3,
  output out_4
);

  wire and_1_out, and_2_out, not_1_out;

  not not_1 (not_1_out, D);
  and and_1 (and_1_out, not_1_out, Clock);
  and and_2 (and_2_out, Clock, D);
  nor nor_1 (out_3, and_1_out, out_4);
  nor nor_2 (out_4, out_3, and_2_out);
endmodule

// PC
module _18_bit_Register (
  input  [17:0] in_1,
  input  Write,
  input  Read,
  output [17:0] out_4
);

  wire and_1_out, and_2_out, and_3_out, and_4_out, and_5_out, and_6_out, and_7_out, and_8_out, and_9_out,
       and_10_out, and_11_out, and_12_out, and_13_out, and_14_out, and_15_out, and_16_out, and_17_out,
       and_18_out;

  and and_1 (and_1_out, Write, in_1[17]);
  and and_2 (and_2_out, Write, in_1[16]);
  D_Flip_Flop d_ff_1 (.D(and_1_out), .Clock(Read), .out_3(out_4[17]));  // open: out_4
  D_Flip_Flop d_ff_2 (.D(and_2_out), .Clock(Read), .out_3(out_4[16]));  // open: out_4
  and and_3 (and_3_out, Write, in_1[15]);
  and and_4 (and_4_out, Write, in_1[14]);
  D_Flip_Flop d_ff_3 (.D(and_3_out), .Clock(Read), .out_3(out_4[15]));  // open: out_4
  and and_5 (and_5_out, Write, in_1[13]);
  D_Flip_Flop d_ff_4 (.D(and_4_out), .Clock(Read), .out_3(out_4[14]));  // open: out_4
  and and_6 (and_6_out, Write, in_1[12]);
  D_Flip_Flop d_ff_5 (.D(and_5_out), .Clock(Read), .out_3(out_4[13]));  // open: out_4
  D_Flip_Flop d_ff_6 (.D(and_6_out), .Clock(Read), .out_3(out_4[12]));  // open: out_4
  and and_7 (and_7_out, Write, in_1[10]);
  and and_8 (and_8_out, Write, in_1[11]);
  D_Flip_Flop d_ff_7 (.D(and_8_out), .Clock(Read), .out_3(out_4[11]));  // open: out_4
  and and_9 (and_9_out, Write, in_1[9]);
  D_Flip_Flop d_ff_8 (.D(and_7_out), .Clock(Read), .out_3(out_4[10]));  // open: out_4
  and and_10 (and_10_out, Write, in_1[8]);
  D_Flip_Flop d_ff_9 (.D(and_10_out), .Clock(Read), .out_3(out_4[8]));  // open: out_4
  D_Flip_Flop d_ff_10 (.D(and_9_out), .Clock(Read), .out_3(out_4[9]));  // open: out_4
  and and_11 (and_11_out, Write, in_1[6]);
  and and_12 (and_12_out, Write, in_1[7]);
  D_Flip_Flop d_ff_11 (.D(and_12_out), .Clock(Read), .out_3(out_4[7]));  // open: out_4
  and and_13 (and_13_out, Write, in_1[5]);
  D_Flip_Flop d_ff_12 (.D(and_11_out), .Clock(Read), .out_3(out_4[6]));  // open: out_4
  and and_14 (and_14_out, Write, in_1[4]);
  D_Flip_Flop d_ff_13 (.D(and_13_out), .Clock(Read), .out_3(out_4[5]));  // open: out_4
  D_Flip_Flop d_ff_14 (.D(and_14_out), .Clock(Read), .out_3(out_4[4]));  // open: out_4
  and and_15 (and_15_out, Write, in_1[3]);
  and and_16 (and_16_out, Write, in_1[2]);
  D_Flip_Flop d_ff_15 (.D(and_15_out), .Clock(Read), .out_3(out_4[3]));  // open: out_4
  and and_17 (and_17_out, Write, in_1[1]);
  D_Flip_Flop d_ff_16 (.D(and_16_out), .Clock(Read), .out_3(out_4[2]));  // open: out_4
  and and_18 (and_18_out, Write, in_1[0]);
  D_Flip_Flop d_ff_17 (.D(and_18_out), .Clock(Read), .out_3(out_4[0]));  // open: out_4
  D_Flip_Flop d_ff_18 (.D(and_17_out), .Clock(Read), .out_3(out_4[1]));  // open: out_4
endmodule

module Register_File (
  input  [3:0] Src_Reg_1,
  input  [3:0] in_2,
  input  [3:0] write_reg,
  input  register_write,
  input  [17:0] write_data,
  output [17:0] out_6
);

  wire and_1_out, and_2_out, and_3_out, and_4_out, and_5_out, and_6_out, and_7_out, and_8_out, and_9_out,
       and_10_out, and_11_out, and_12_out, and_13_out, and_14_out, and_15_out, and_16_out, decoder_1_out0,
       decoder_1_out1, decoder_1_out2, decoder_1_out3, decoder_1_out4, decoder_1_out5, decoder_1_out6,
       decoder_1_out7, decoder_1_out8, decoder_1_out9, decoder_1_out10, decoder_1_out11, decoder_1_out12,
       decoder_1_out13, decoder_1_out14, decoder_1_out15, decoder_2_out0, decoder_2_out1, decoder_2_out2,
       decoder_2_out3, decoder_2_out4, decoder_2_out5, decoder_2_out6, decoder_2_out7, decoder_2_out8,
       decoder_2_out9, decoder_2_out10, decoder_2_out11, decoder_2_out12, decoder_2_out13, decoder_2_out14,
       decoder_2_out15;
  wire [17:0] R0_out_4, R1_out_4, R2_out_4, R3_out_4, R4_out_4, R5_out_4, R6_out_4, R7_out_4, R8_out_4,
       R9_out_4, R10_out_4, R11_out_4, R12_out_4, R13_out_4, R14_out_4, R15_out_4;

  Decoder #(.select(4), .enable("false")) decoder_1 (
    .out0(decoder_1_out0), .out1(decoder_1_out1), .out2(decoder_1_out2), .out3(decoder_1_out3),
    .out4(decoder_1_out4), .out5(decoder_1_out5), .out6(decoder_1_out6), .out7(decoder_1_out7),
    .out8(decoder_1_out8), .out9(decoder_1_out9), .out10(decoder_1_out10), .out11(decoder_1_out11),
    .out12(decoder_1_out12), .out13(decoder_1_out13), .out14(decoder_1_out14), .out15(decoder_1_out15),
    .sel(in_2));
  Decoder #(.select(4), .enable("false")) decoder_2 (
    .out0(decoder_2_out0), .out1(decoder_2_out1), .out2(decoder_2_out2), .out3(decoder_2_out3),
    .out4(decoder_2_out4), .out5(decoder_2_out5), .out6(decoder_2_out6), .out7(decoder_2_out7),
    .out8(decoder_2_out8), .out9(decoder_2_out9), .out10(decoder_2_out10), .out11(decoder_2_out11),
    .out12(decoder_2_out12), .out13(decoder_2_out13), .out14(decoder_2_out14), .out15(decoder_2_out15),
    .sel(write_reg));
  and and_1 (and_1_out, decoder_2_out0, register_write);
  and and_2 (and_2_out, decoder_2_out1, register_write);
  and and_3 (and_3_out, decoder_2_out2, register_write);
  and and_4 (and_4_out, decoder_2_out3, register_write);
  and and_5 (and_5_out, decoder_2_out4, register_write);
  and and_6 (and_6_out, decoder_2_out5, register_write);
  and and_7 (and_7_out, decoder_2_out6, register_write);
  and and_8 (and_8_out, decoder_2_out7, register_write);
  and and_9 (and_9_out, decoder_2_out8, register_write);
  and and_10 (and_10_out, decoder_2_out9, register_write);
  and and_11 (and_11_out, decoder_2_out10, register_write);
  and and_12 (and_12_out, decoder_2_out11, register_write);
  and and_13 (and_13_out, decoder_2_out12, register_write);
  and and_14 (and_14_out, decoder_2_out13, register_write);
  and and_15 (and_15_out, decoder_2_out14, register_write);
  and and_16 (and_16_out, decoder_2_out15, register_write);
  _18_bit_Register R0 (.in_1(write_data), .Read(decoder_1_out0), .out_4(R0_out_4), .Write(and_1_out));
  _18_bit_Register R1 (.in_1(write_data), .Read(decoder_1_out1), .out_4(R1_out_4), .Write(and_2_out));
  _18_bit_Register R2 (.in_1(write_data), .Read(decoder_1_out2), .out_4(R2_out_4), .Write(and_3_out));
  _18_bit_Register R3 (.in_1(write_data), .Read(decoder_1_out3), .out_4(R3_out_4), .Write(and_4_out));
  _18_bit_Register R4 (.in_1(write_data), .Read(decoder_1_out4), .out_4(R4_out_4), .Write(and_5_out));
  _18_bit_Register R5 (.in_1(write_data), .Read(decoder_1_out5), .out_4(R5_out_4), .Write(and_6_out));
  _18_bit_Register R6 (.in_1(write_data), .Read(decoder_1_out6), .out_4(R6_out_4), .Write(and_7_out));
  _18_bit_Register R7 (.in_1(write_data), .Read(decoder_1_out7), .out_4(R7_out_4), .Write(and_8_out));
  _18_bit_Register R8 (.in_1(write_data), .Read(decoder_1_out8), .out_4(R8_out_4), .Write(and_9_out));
  _18_bit_Register R9 (.in_1(write_data), .Read(decoder_1_out9), .out_4(R9_out_4), .Write(and_10_out));
  _18_bit_Register R10 (.in_1(write_data), .Read(decoder_1_out10), .out_4(R10_out_4), .Write(and_11_out));
  _18_bit_Register R11 (.in_1(write_data), .Read(decoder_1_out11), .out_4(R11_out_4), .Write(and_12_out));
  _18_bit_Register R12 (.in_1(write_data), .Read(decoder_1_out12), .out_4(R12_out_4), .Write(and_13_out));
  _18_bit_Register R13 (.in_1(write_data), .Read(decoder_1_out13), .out_4(R13_out_4), .Write(and_14_out));
  _18_bit_Register R14 (.in_1(write_data), .Read(decoder_1_out14), .out_4(R14_out_4), .Write(and_15_out));
  _18_bit_Register R15 (.in_1(write_data), .Read(decoder_1_out15), .out_4(R15_out_4), .Write(and_16_out));
  Multiplexer #(.select(4), .width(18), .enable("false")) multiplexer_1 (
    .in0(R0_out_4), .in1(R1_out_4), .in2(R2_out_4), .in3(R3_out_4), .in4(R4_out_4), .in5(R5_out_4),
    .in6(R6_out_4), .in7(R7_out_4), .in8(R8_out_4), .in9(R9_out_4), .in10(R10_out_4), .in11(R11_out_4),
    .in12(R12_out_4), .in13(R13_out_4), .in14(R14_out_4), .in15(R15_out_4), .out(out_6), .sel(Src_Reg_1));
endmodule

module ALU__Arithmetic_Logic_Unit (
  input  [17:0] Input1,
  input  [1:0] Select,
  input  [17:0] Input2,
  output [17:0] Output
);

  wire [17:0] and_1_out, multiplexer_1_out, nand_1_out, nor_1_out, reg_adder_1_out_3;

  // Probe on Input1
  Reg_Adder reg_adder_1 (.out_3(reg_adder_1_out_3), .Reg_1(Input2), .Reg_2(Input1));
  assign and_1_out = Input1 & Input2;  // AND_Gate and_1, 18 bits wide
  assign nand_1_out = ~(Input1 & Input2);  // NAND_Gate nand_1, 18 bits wide
  assign nor_1_out = ~(Input1 | Input2);  // NOR_Gate nor_1, 18 bits wide
  Multiplexer #(.select(2), .width(18), .enable("false")) multiplexer_1 (
    .in0(reg_adder_1_out_3), .in1(and_1_out), .in2(nand_1_out), .in3(nor_1_out), .out(multiplexer_1_out),
    .sel(Select));
  Bit_Extender #(.in_width(18), .out_width(18)) bit_extender_1 (.in(multiplexer_1_out), .out(Output));
endmodule

module Half_Adder (
  input  in_1,
  input  in_2,
  output Cout,
  output S
);

  and and_1 (Cout, in_1, in_2);
  xor xor_1 (S, in_1, in_2);
endmodule

module Reg_Adder (
  input  [17:0] Reg_2,
  input  [17:0] Reg_1,
  output [17:0] out_3
);

  wire full_adder_1_cout, full_adder_2_cout, full_adder_3_cout, full_adder_4_cout, full_adder_5_cout,
       full_adder_6_cout, full_adder_7_cout, full_adder_8_cout, full_adder_9_cout, full_adder_10_cout,
       full_adder_12_cout, full_adder_13_cout, full_adder_14_cout, full_adder_15_cout, full_adder_16_cout,
       full_adder_17_cout, half_adder_1_cout;

  Full_Adder full_adder_1 (
    .i0(Reg_1[9]), .i1(Reg_2[16]), .Cin(full_adder_3_cout), .Sum(out_3[9]), .Cout(full_adder_1_cout));
  Full_Adder full_adder_2 (
    .i0(Reg_1[7]), .i1(Reg_2[7]), .Cin(full_adder_5_cout), .Sum(out_3[7]), .Cout(full_adder_2_cout));
  Full_Adder full_adder_3 (
    .i0(Reg_1[8]), .i1(Reg_2[17]), .Cin(full_adder_2_cout), .Sum(out_3[8]), .Cout(full_adder_3_cout));
  Full_Adder full_adder_4 (
    .i0(Reg_1[5]), .i1(Reg_2[5]), .Cin(full_adder_7_cout), .Sum(out_3[5]), .Cout(full_adder_4_cout));
  Full_Adder full_adder_5 (
    .i0(Reg_1[6]), .i1(Reg_2[6]), .Cin(full_adder_4_cout), .Sum(out_3[6]), .Cout(full_adder_5_cout));
  Full_Adder full_adder_6 (
    .i0(Reg_1[3]), .i1(Reg_2[3]), .Cin(full_adder_9_cout), .Sum(out_3[3]), .Cout(full_adder_6_cout));
  Full_Adder full_adder_7 (
    .i0(Reg_1[4]), .i1(Reg_2[4]), .Cin(full_adder_6_cout), .Sum(out_3[4]), .Cout(full_adder_7_cout));
  Full_Adder full_adder_8 (
    .i0(Reg_1[1]), .i1(Reg_2[1]), .Cin(half_adder_1_cout), .Sum(out_3[1]), .Cout(full_adder_8_cout));
  Full_Adder full_adder_9 (
    .i0(Reg_1[2]), .i1(Reg_2[2]), .Cin(full_adder_8_cout), .Sum(out_3[2]), .Cout(full_adder_9_cout));
  Half_Adder half_adder_1 (.in_1(Reg_1[0]), .in_2(Reg_2[0]), .Cout(half_adder_1_cout), .S(out_3[0]));
  Full_Adder full_adder_10 (
    .i0(Reg_1[16]), .i1(Reg_2[16]), .Cin(full_adder_13_cout), .Sum(out_3[16]), .Cout(full_adder_10_cout));
  Full_Adder full_adder_11 (.i0(Reg_1[17]), .i1(Reg_2[17]), .Cin(full_adder_10_cout), .Sum(out_3[17]));  // open: Cout
  Full_Adder full_adder_12 (
    .i0(Reg_1[14]), .i1(Reg_2[14]), .Cin(full_adder_15_cout), .Sum(out_3[14]), .Cout(full_adder_12_cout));
  Full_Adder full_adder_13 (
    .i0(Reg_1[15]), .i1(Reg_2[15]), .Cin(full_adder_12_cout), .Sum(out_3[15]), .Cout(full_adder_13_cout));
  Full_Adder full_adder_14 (
    .i0(Reg_1[12]), .i1(Reg_2[12]), .Cin(full_adder_17_cout), .Sum(out_3[12]), .Cout(full_adder_14_cout));
  Full_Adder full_adder_15 (
    .i0(Reg_1[13]), .i1(Reg_2[13]), .Cin(full_adder_14_cout), .Sum(out_3[13]), .Cout(full_adder_15_cout));
  Full_Adder full_adder_16 (
    .i0(Reg_1[10]), .i1(Reg_2[10]), .Cin(full_adder_1_cout), .Sum(out_3[10]), .Cout(full_adder_16_cout));
  Full_Adder full_adder_17 (
    .i0(Reg_1[11]), .i1(Reg_2[11]), .Cin(full_adder_16_cout), .Sum(out_3[11]), .Cout(full_adder_17_cout));

  assign Reg_2[9:8] = {Reg_2[16], Reg_2[17]};
endmodule

module Full_Adder (
  input  i0,
  input  i1,
  input  Cin,
  output Sum,
  output Cout
);

  wire and_1_out, and_2_out, xor_1_out;

  xor xor_1 (xor_1_out, i0, i1);
  xor xor_2 (Sum, xor_1_out, Cin);
  and and_1 (and_1_out, xor_1_out, Cin);
  or or_1 (Cout, and_1_out, and_2_out);
  and and_2 (and_2_out, i0, i1);
endmodule

module Memory_File (
);

  _18_bit_Register u_18_bit_register_1 ();  // open: in_1, Read, out_4, Write
endmodule

module CMP_Unit (
);

  _18_bit_Register u_18_bit_register_1 ();  // open: in_1, Read, out_4, Write
  _18_bit_Register u_18_bit_register_2 ();  // open: in_1, Read, out_4, Write
  _18_bit_Register u_18_bit_register_3 ();  // open: in_1, Read, out_4, Write
  _18_bit_Register u_18_bit_register_4 ();  // open: in_1, Read, out_4, Write
endmodule

module _10_bit_Register (
  input  [9:0] in_1,
  input  Write,
  input  Read,
  output [9:0] out_4
);

  wire and_1_out, and_2_out, and_3_out, and_4_out, and_5_out, and_6_out, and_7_out, and_8_out, and_9_out,
       and_10_out;

  and and_1 (and_1_out, Write, in_1[9]);
  and and_2 (and_2_out, Write, in_1[8]);
  D_Flip_Flop d_ff_1 (.D(and_1_out), .Clock(Read), .out_3(out_4[9]));  // open: out_4
  D_Flip_Flop d_ff_2 (.D(and_2_out), .Clock(Read), .out_3(out_4[8]));  // open: out_4
  and and_3 (and_3_out, Write, in_1[7]);
  and and_4 (and_4_out, Write, in_1[6]);
  D_Flip_Flop d_ff_3 (.D(and_3_out), .Clock(Read), .out_3(out_4[7]));  // open: out_4
  and and_5 (and_5_out, Write, in_1[5]);
  D_Flip_Flop d_ff_4 (.D(and_4_out), .Clock(Read), .out_3(out_4[6]));  // open: out_4
  and and_6 (and_6_out, Write, in_1[4]);
  D_Flip_Flop d_ff_5 (.D(and_5_out), .Clock(Read), .out_3(out_4[5]));  // open: out_4
  D_Flip_Flop d_ff_6 (.D(and_6_out), .Clock(Read), .out_3(out_4[4]));  // open: out_4
  and and_7 (and_7_out, Write, in_1[2]);
  and and_8 (and_8_out, Write, in_1[3]);
  D_Flip_Flop d_ff_7 (.D(and_8_out), .Clock(Read), .out_3(out_4[3]));  // open: out_4
  and and_9 (and_9_out, Write, in_1[1]);
  D_Flip_Flop d_ff_8 (.D(and_7_out), .Clock(Read), .out_3(out_4[2]));  // open: out_4
  and and_10 (and_10_out, Write, in_1[0]);
  D_Flip_Flop d_ff_9 (.D(and_10_out), .Clock(Read), .out_3(out_4[0]));  // open: out_4
  D_Flip_Flop d_ff_10 (.D(and_9_out), .Clock(Read), .out_3(out_4[1]));  // open: out_4
endmodule
