// Logisim project CPU.circ as structural Verilog: 29 circuits, main circuit main
module main (
);

  wire alu, branch, Clock, comparison, controlled_buffer_1_out, dataMemRead, dataMemWrite, enableJump,
       enablePC, enableWrite, jump, multiplexer_1_out, multiplexer_4_out, nextInst, or_1_out, or_2_out,
       regWrite, Reset;
  wire [1:0] ALUcontrol;
  wire [3:0] DEST_SRC_OP1, multiplexer_2_out, SRC1_OP2, SRC2;
  wire [9:0] JumpAddress, LD_ST_Address, program_counter_pc_1_output;
  wire [13:0] control_unit_1_address_14;
  wire [17:0] ALUresult, dataMemResult, multiplexer_3_out, REG1_data, REG2_data, REG2_data_new, rom_1_data;

  or or_1 (or_1_out, nextInst, enableJump);
  Clock clock_1 (.out(Clock));
  Button button_1 (.out(Reset));
  Multiplexer #(.enable("false")) multiplexer_1 (.in0(1'b0), .in1(Clock), .out(multiplexer_1_out), .sel(or_1_out));
  Program_Counter_PC program_counter_pc_1 (
    .next(enableJump), .enableJump(nextInst), .branch(branch), .clock(controlled_buffer_1_out),
    .reset(Reset), .JumpAddress(JumpAddress), .\output (program_counter_pc_1_output));  // open: BranchAddress
  assign controlled_buffer_1_out = enablePC ? multiplexer_1_out : 1'bz;  // Controlled_Buffer controlled_buffer_1
  ALU__Arithmetic_Logic_Unit alu_arithmetic_logic_unit_1 (
    .Input2(REG2_data_new), .in_4(alu), .Input1(REG1_data), .Select(ALUcontrol), .Output(ALUresult));
  FSM fsm_1 (
    .clock(Clock), .LD(dataMemRead), .ST(dataMemWrite), .jump(jump), .compraison(comparison), .alu(alu),
    .enableWrite(enableWrite), .enablePC(enablePC), .nextInst(nextInst), .enableJump(enableJump));
  ROM #(.addrWidth(10), .dataWidth(18)) rom_1 (.addr(program_counter_pc_1_output), .data(rom_1_data));  // open: sel
  Control_Unit control_unit_1 (
    ._18_bit_input(rom_1_data), .reg1(REG1_data), .reg2(REG2_data), .SRC_DEST_OP1(DEST_SRC_OP1),
    .SRC1_OP2(SRC1_OP2), .SRC2(SRC2), .ALU_operation(ALUcontrol), .alu(alu), .ADDREESS10(LD_ST_Address),
    .regWrite(regWrite), .ADDRESS_14(control_unit_1_address_14), .jumpCond(branch), .comparison(comparison),
    .REG2_data_new(REG2_data_new), .dataMemRead(dataMemRead), .dataMemWrite(dataMemWrite), .jump(jump));  // open: immSig, IMM_ADDRESS6
  Bit_Extender #(.in_width(14), .out_width(10)) bit_extender_1 (.in(control_unit_1_address_14), .out(JumpAddress));
  Multiplexer #(.width(4), .enable("false")) multiplexer_2 (
    .in0(SRC2), .in1(DEST_SRC_OP1), .out(multiplexer_2_out), .sel(or_2_out));
  or or_2 (or_2_out, dataMemWrite, comparison);
  Multiplexer #(.width(18), .enable("false")) multiplexer_3 (
    .in0(ALUresult), .in1(dataMemResult), .out(multiplexer_3_out), .sel(dataMemRead));
  Register_File register_file_1 (
    .Src_Data_1(REG1_data), .Src_Data_2(REG2_data), .Dest_Reg(DEST_SRC_OP1),
    .write_enable(multiplexer_4_out), .write_data(multiplexer_3_out), .Src_Reg_1(SRC1_OP2),
    .Src_Reg_2(multiplexer_2_out), .clk(Clock));
  Multiplexer #(.enable("false")) multiplexer_4 (
    .in0(1'b0), .in1(regWrite), .out(multiplexer_4_out), .sel(enableWrite));
  RAM #(.addrWidth(10), .dataWidth(18), .bus("separate")) ram_1 (
    .addr(LD_ST_Address), .din(REG2_data_new), .data(dataMemResult), .str(dataMemWrite), .sel(1'b1),
    .clk(Clock), .ld(dataMemRead));  // open: clr

  // Notes on the sheet:
  //   contents of rom_1 (hex, n*v repeats v):
  //   1408 10c4c 1940c 1d9c8 21c08 28064 2c065 3006e 3406f 383e8 24003 66ac f378 2fc14 14653
endmodule

module D_Latch (
  input  D,
  input  Clock,
  output out_3,
  output out_4
);

  wire and_1_out, and_2_out, not_1_out;

  not not_1 (not_1_out, D);
  and and_1 (and_1_out, not_1_out, Clock);
  and and_2 (and_2_out, Clock, D);
  nor nor_1 (out_3, and_1_out, out_4);
  nor nor_2 (out_4, out_3, and_2_out);
endmodule

module _18_bit_Register (
  input  [17:0] in_1,
  input  load,
  output [17:0] out_3
);

  Dflipflop dflipflop_1 (.data(in_1[17]), .clk(load), .out_3(out_3[17]));
  Dflipflop dflipflop_2 (.data(in_1[15]), .clk(load), .out_3(out_3[15]));
  Dflipflop dflipflop_3 (.data(in_1[16]), .clk(load), .out_3(out_3[16]));
  Dflipflop dflipflop_4 (.data(in_1[14]), .clk(load), .out_3(out_3[14]));
  Dflipflop dflipflop_5 (.data(in_1[13]), .clk(load), .out_3(out_3[13]));
  Dflipflop dflipflop_6 (.data(in_1[12]), .clk(load), .out_3(out_3[12]));
  Dflipflop dflipflop_7 (.data(in_1[10]), .clk(load), .out_3(out_3[10]));
  Dflipflop dflipflop_8 (.data(in_1[9]), .clk(load), .out_3(out_3[9]));
  Dflipflop dflipflop_9 (.data(in_1[11]), .clk(load), .out_3(out_3[11]));
  Dflipflop dflipflop_10 (.data(in_1[6]), .clk(load), .out_3(out_3[6]));
  Dflipflop dflipflop_11 (.data(in_1[7]), .clk(load), .out_3(out_3[7]));
  Dflipflop dflipflop_12 (.data(in_1[8]), .clk(load), .out_3(out_3[8]));
  Dflipflop dflipflop_13 (.data(in_1[4]), .clk(load), .out_3(out_3[4]));
  Dflipflop dflipflop_14 (.data(in_1[5]), .clk(load), .out_3(out_3[5]));
  Dflipflop dflipflop_15 (.data(in_1[3]), .clk(load), .out_3(out_3[3]));
  Dflipflop dflipflop_16 (.data(in_1[2]), .clk(load), .out_3(out_3[2]));
  Dflipflop dflipflop_17 (.data(in_1[1]), .clk(load), .out_3(out_3[1]));
  Dflipflop dflipflop_18 (.data(in_1[0]), .clk(load), .out_3(out_3[0]));
endmodule

// ALU
module ALU__Arithmetic_Logic_Unit (
  input  [17:0] Input1,
  input  [1:0] Select,
  input  [17:0] Input2,
  input  in_4,
  output [17:0] Output
);

  wire [17:0] addgate_1_out_5, andgate_1_out_5, nandgate_1_out_3, norgate_1_out_3;

  addGate addgate_1 (
    .regData1(Input1), .regData2(Input2), ._16th_bit(in_4), .out_5(addgate_1_out_5));  // open: immValue
  andGate andgate_1 (
    .regData1(Input1), .regData2(Input2), ._16th_bit(in_4), .out_5(andgate_1_out_5));  // open: immValue
  nandGate nandgate_1 (.regData1(Input1), .regData2(Input2), .out_3(nandgate_1_out_3));
  norGate norgate_1 (.regData1(Input1), .regData2(Input2), .out_3(norgate_1_out_3));
  Multiplexer #(.select(2), .width(18), .enable("false")) multiplexer_1 (
    .in0(addgate_1_out_5), .in1(andgate_1_out_5), .in2(nandgate_1_out_3), .in3(norgate_1_out_3),
    .out(Output), .sel(Select));
  // Probe on Output
endmodule

module Half_Adder (
  input  in_1,
  input  in_2,
  output Cout,
  output S
);

  and and_1 (Cout, in_1, in_2);
  xor xor_1 (S, in_1, in_2);
endmodule

module _18_bit_Adder (
  input  [17:0] Reg_2,
  input  [17:0] Reg_1,
  output [17:0] out_3
);

  wire full_adder_1_cout, full_adder_2_cout, full_adder_3_cout, full_adder_4_cout, full_adder_5_cout,
       full_adder_6_cout, full_adder_7_cout, full_adder_8_cout, full_adder_9_cout, full_adder_10_cout,
       full_adder_12_cout, full_adder_13_cout, full_adder_14_cout, full_adder_15_cout, full_adder_16_cout,
       full_adder_17_cout, half_adder_1_cout;

  Full_Adder full_adder_1 (
    .i0(Reg_1[9]), .i1(Reg_2[9]), .Cin(full_adder_3_cout), .Sum(out_3[9]), .Cout(full_adder_1_cout));
  Full_Adder full_adder_2 (
    .i0(Reg_1[7]), .i1(Reg_2[7]), .Cin(full_adder_5_cout), .Sum(out_3[7]), .Cout(full_adder_2_cout));
  Full_Adder full_adder_3 (
    .i0(Reg_1[8]), .i1(Reg_2[8]), .Cin(full_adder_2_cout), .Sum(out_3[8]), .Cout(full_adder_3_cout));
  Full_Adder full_adder_4 (
    .i0(Reg_1[5]), .i1(Reg_2[5]), .Cin(full_adder_7_cout), .Sum(out_3[5]), .Cout(full_adder_4_cout));
  Full_Adder full_adder_5 (
    .i0(Reg_1[6]), .i1(Reg_2[6]), .Cin(full_adder_4_cout), .Sum(out_3[6]), .Cout(full_adder_5_cout));
  Full_Adder full_adder_6 (
    .i0(Reg_1[3]), .i1(Reg_2[3]), .Cin(full_adder_9_cout), .Sum(out_3[3]), .Cout(full_adder_6_cout));
  Full_Adder full_adder_7 (
    .i0(Reg_1[4]), .i1(Reg_2[4]), .Cin(full_adder_6_cout), .Sum(out_3[4]), .Cout(full_adder_7_cout));
  Full_Adder full_adder_8 (
    .i0(Reg_1[1]), .i1(Reg_2[1]), .Cin(half_adder_1_cout), .Sum(out_3[1]), .Cout(full_adder_8_cout));
  Full_Adder full_adder_9 (
    .i0(Reg_1[2]), .i1(Reg_2[2]), .Cin(full_adder_8_cout), .Sum(out_3[2]), .Cout(full_adder_9_cout));
  Half_Adder half_adder_1 (.in_1(Reg_1[0]), .in_2(Reg_2[0]), .Cout(half_adder_1_cout), .S(out_3[0]));
  Full_Adder full_adder_10 (
    .i0(Reg_1[16]), .i1(Reg_2[16]), .Cin(full_adder_13_cout), .Sum(out_3[16]), .Cout(full_adder_10_cout));
  Full_Adder full_adder_11 (.i0(Reg_1[17]), .i1(Reg_2[17]), .Cin(full_adder_10_cout), .Sum(out_3[17]));  // open: Cout
  Full_Adder full_adder_12 (
    .i0(Reg_1[14]), .i1(Reg_2[14]), .Cin(full_adder_15_cout), .Sum(out_3[14]), .Cout(full_adder_12_cout));
  Full_Adder full_adder_13 (
    .i0(Reg_1[15]), .i1(Reg_2[15]), .Cin(full_adder_12_cout), .Sum(out_3[15]), .Cout(full_adder_13_cout));
  Full_Adder full_adder_14 (
    .i0(Reg_1[12]), .i1(Reg_2[12]), .Cin(full_adder_17_cout), .Sum(out_3[12]), .Cout(full_adder_14_cout));
  Full_Adder full_adder_15 (
    .i0(Reg_1[13]), .i1(Reg_2[13]), .Cin(full_adder_14_cout), .Sum(out_3[13]), .Cout(full_adder_15_cout));
  Full_Adder full_adder_16 (
    .i0(Reg_1[10]), .i1(Reg_2[10]), .Cin(full_adder_1_cout), .Sum(out_3[10]), .Cout(full_adder_16_cout));
  Full_Adder full_adder_17 (
    .i0(Reg_1[11]), .i1(Reg_2[11]), .Cin(full_adder_16_cout), .Sum(out_3[11]), .Cout(full_adder_17_cout));
endmodule

module Full_Adder (
  input  i0,
  input  i1,
  input  Cin,
  output Sum,
  output Cout
);

  wire and_1_out, and_2_out, xor_1_out;

  xor xor_1 (xor_1_out, i0, i1);
  xor xor_2 (Sum, xor_1_out, Cin);
  and and_1 (and_1_out, xor_1_out, Cin);
  or or_1 (Cout, and_1_out, and_2_out);
  and and_2 (and_2_out, i0, i1);
endmodule

module JUMP_Unit (
  input  [12:0] immediate,
  input  Enable,
  input  [9:0] PC,
  input  in_4,
  input  in_5,
  output [9:0] out_6
);

  wire [9:0] bit_extender_1_out, n10_bit_adder_1_out_3, program_counter_pc_1_p4;

  Bit_Extender #(.in_width(13), .out_width(10)) bit_extender_1 (.in(immediate), .out(bit_extender_1_out));
  // Program_Counter_PC program_counter_pc_1: pin names not known; wires that end beside it: PC, in_4, in_5, program_counter_pc_1_p4
  _10_bit_adder u_10_bit_adder_1 (
    .out_3(n10_bit_adder_1_out_3), .PC_2(program_counter_pc_1_p4), .PC(bit_extender_1_out));
  assign out_6 = Enable ? n10_bit_adder_1_out_3 : 10'bz;  // Controlled_Buffer controlled_buffer_1
endmodule

module CMP_Unit (
  input  [17:0] in_1,
  input  [17:0] in_2,
  output eq,
  output gt,
  output lt
);

  wire full_cmp_1_eq_2, full_cmp_1_g, full_cmp_1_lt_2, full_cmp_2_eq_2, full_cmp_2_g, full_cmp_2_lt_2,
       full_cmp_3_eq_2, full_cmp_3_g, full_cmp_3_lt_2, full_cmp_4_eq_2, full_cmp_4_g, full_cmp_4_lt_2,
       full_cmp_5_eq_2, full_cmp_5_g, full_cmp_5_lt_2, full_cmp_6_eq_2, full_cmp_6_g, full_cmp_6_lt_2,
       full_cmp_7_eq_2, full_cmp_7_g, full_cmp_7_lt_2, full_cmp_8_eq_2, full_cmp_8_g, full_cmp_8_lt_2,
       full_cmp_9_eq_2, full_cmp_9_g, full_cmp_9_lt_2, full_cmp_10_eq_2, full_cmp_10_g, full_cmp_10_lt_2,
       full_cmp_11_eq_2, full_cmp_11_g, full_cmp_11_lt_2, full_cmp_12_eq_2, full_cmp_12_g, full_cmp_12_lt_2,
       full_cmp_13_eq_2, full_cmp_13_g, full_cmp_13_lt_2, full_cmp_14_eq_2, full_cmp_14_g, full_cmp_14_lt_2,
       full_cmp_15_eq_2, full_cmp_15_g, full_cmp_15_lt_2, full_cmp_17_eq_2, full_cmp_17_g, full_cmp_17_lt_2,
       half_cmp_1_eq, half_cmp_1_gt, half_cmp_1_lt;

  half_cmp half_cmp_1 (.a(in_1[17]), .b(in_2[17]), .eq(half_cmp_1_eq), .gt(half_cmp_1_gt), .lt(half_cmp_1_lt));
  full_cmp full_cmp_1 (
    .a(in_1[16]), .b(in_2[16]), .gt(half_cmp_1_gt), .lt(half_cmp_1_lt), .eq(half_cmp_1_eq), .g(full_cmp_1_g),
    .lt_2(full_cmp_1_lt_2), .eq_2(full_cmp_1_eq_2));
  full_cmp full_cmp_2 (
    .a(in_1[15]), .b(in_2[15]), .gt(full_cmp_1_g), .lt(full_cmp_1_lt_2), .eq(full_cmp_1_eq_2),
    .g(full_cmp_2_g), .lt_2(full_cmp_2_lt_2), .eq_2(full_cmp_2_eq_2));
  full_cmp full_cmp_3 (
    .a(in_1[14]), .b(in_2[14]), .gt(full_cmp_2_g), .lt(full_cmp_2_lt_2), .eq(full_cmp_2_eq_2),
    .g(full_cmp_3_g), .lt_2(full_cmp_3_lt_2), .eq_2(full_cmp_3_eq_2));
  full_cmp full_cmp_4 (
    .a(in_1[13]), .b(in_2[13]), .gt(full_cmp_3_g), .lt(full_cmp_3_lt_2), .eq(full_cmp_3_eq_2),
    .g(full_cmp_4_g), .lt_2(full_cmp_4_lt_2), .eq_2(full_cmp_4_eq_2));
  full_cmp full_cmp_5 (
    .a(in_1[12]), .b(in_2[12]), .gt(full_cmp_4_g), .lt(full_cmp_4_lt_2), .eq(full_cmp_4_eq_2),
    .g(full_cmp_5_g), .lt_2(full_cmp_5_lt_2), .eq_2(full_cmp_5_eq_2));
  full_cmp full_cmp_6 (
    .a(in_1[11]), .b(in_2[11]), .gt(full_cmp_5_g), .lt(full_cmp_5_lt_2), .eq(full_cmp_5_eq_2),
    .g(full_cmp_6_g), .lt_2(full_cmp_6_lt_2), .eq_2(full_cmp_6_eq_2));
  full_cmp full_cmp_7 (
    .a(in_1[10]), .b(in_2[10]), .gt(full_cmp_6_g), .lt(full_cmp_6_lt_2), .eq(full_cmp_6_eq_2),
    .g(full_cmp_7_g), .lt_2(full_cmp_7_lt_2), .eq_2(full_cmp_7_eq_2));
  full_cmp full_cmp_8 (
    .a(in_1[8]), .b(in_2[8]), .gt(full_cmp_9_g), .lt(full_cmp_9_lt_2), .eq(full_cmp_9_eq_2),
    .g(full_cmp_8_g), .lt_2(full_cmp_8_lt_2), .eq_2(full_cmp_8_eq_2));
  full_cmp full_cmp_9 (
    .a(in_1[9]), .b(in_2[9]), .gt(full_cmp_7_g), .lt(full_cmp_7_lt_2), .eq(full_cmp_7_eq_2),
    .g(full_cmp_9_g), .lt_2(full_cmp_9_lt_2), .eq_2(full_cmp_9_eq_2));
  full_cmp full_cmp_10 (
    .a(in_1[7]), .b(in_2[7]), .gt(full_cmp_8_g), .lt(full_cmp_8_lt_2), .eq(full_cmp_8_eq_2),
    .g(full_cmp_10_g), .lt_2(full_cmp_10_lt_2), .eq_2(full_cmp_10_eq_2));
  full_cmp full_cmp_11 (
    .a(in_1[6]), .b(in_2[6]), .gt(full_cmp_10_g), .lt(full_cmp_10_lt_2), .eq(full_cmp_10_eq_2),
    .g(full_cmp_11_g), .lt_2(full_cmp_11_lt_2), .eq_2(full_cmp_11_eq_2));
  full_cmp full_cmp_12 (
    .a(in_1[5]), .b(in_2[5]), .gt(full_cmp_11_g), .lt(full_cmp_11_lt_2), .eq(full_cmp_11_eq_2),
    .g(full_cmp_12_g), .lt_2(full_cmp_12_lt_2), .eq_2(full_cmp_12_eq_2));
  full_cmp full_cmp_13 (
    .a(in_1[4]), .b(in_2[4]), .gt(full_cmp_12_g), .lt(full_cmp_12_lt_2), .eq(full_cmp_12_eq_2),
    .g(full_cmp_13_g), .lt_2(full_cmp_13_lt_2), .eq_2(full_cmp_13_eq_2));
  full_cmp full_cmp_14 (
    .a(in_1[3]), .b(in_2[3]), .gt(full_cmp_13_g), .lt(full_cmp_13_lt_2), .eq(full_cmp_13_eq_2),
    .g(full_cmp_14_g), .lt_2(full_cmp_14_lt_2), .eq_2(full_cmp_14_eq_2));
  full_cmp full_cmp_15 (
    .a(in_1[2]), .b(in_2[2]), .gt(full_cmp_14_g), .lt(full_cmp_14_lt_2), .eq(full_cmp_14_eq_2),
    .g(full_cmp_15_g), .lt_2(full_cmp_15_lt_2), .eq_2(full_cmp_15_eq_2));
  full_cmp full_cmp_16 (
    .a(in_1[0]), .b(in_2[0]), .gt(full_cmp_17_g), .lt(full_cmp_17_lt_2), .eq(full_cmp_17_eq_2), .g(gt),
    .lt_2(lt), .eq_2(eq));
  full_cmp full_cmp_17 (
    .a(in_1[1]), .b(in_2[1]), .gt(full_cmp_15_g), .lt(full_cmp_15_lt_2), .eq(full_cmp_15_eq_2),
    .g(full_cmp_17_g), .lt_2(full_cmp_17_lt_2), .eq_2(full_cmp_17_eq_2));
endmodule

module _10_bit_Register (
  input  [9:0] in_1,
  input  load,
  output [9:0] out_3
);

  Dflipflop dflipflop_1 (.data(in_1[9]), .clk(load), .out_3(out_3[9]));
  Dflipflop dflipflop_2 (.data(in_1[8]), .clk(load), .out_3(out_3[8]));
  Dflipflop dflipflop_3 (.data(in_1[7]), .clk(load), .out_3(out_3[7]));
  Dflipflop dflipflop_4 (.data(in_1[6]), .clk(load), .out_3(out_3[6]));
  Dflipflop dflipflop_5 (.data(in_1[5]), .clk(load), .out_3(out_3[5]));
  Dflipflop dflipflop_6 (.data(in_1[4]), .clk(load), .out_3(out_3[4]));
  Dflipflop dflipflop_7 (.data(in_1[3]), .clk(load), .out_3(out_3[3]));
  Dflipflop dflipflop_8 (.data(in_1[2]), .clk(load), .out_3(out_3[2]));
  Dflipflop dflipflop_9 (.data(in_1[1]), .clk(load), .out_3(out_3[1]));
  Dflipflop dflipflop_10 (.data(in_1[0]), .clk(load), .out_3(out_3[0]));
endmodule

module Register_File (
  input  [3:0] Dest_Reg,
  input  [3:0] Src_Reg_1,
  input  write_enable,
  input  [17:0] write_data,
  input  clk,
  input  [3:0] Src_Reg_2,
  output [17:0] Src_Data_1,
  output [17:0] Src_Data_2
);

  wire and_1_out, and_2_out, and_3_out, and_4_out, and_5_out, and_6_out, and_7_out, and_8_out, and_9_out,
       and_10_out, and_11_out, and_12_out, and_13_out, and_14_out, and_15_out, and_16_out, and_17_out,
       and_18_out, and_19_out, and_20_out, and_21_out, and_22_out, and_23_out, and_24_out, and_25_out,
       and_26_out, and_27_out, and_28_out, and_29_out, and_30_out, and_31_out, and_32_out, decoder_1_out0,
       decoder_1_out1, decoder_1_out2, decoder_1_out3, decoder_1_out4, decoder_1_out5, decoder_1_out6,
       decoder_1_out7, decoder_1_out8, decoder_1_out9, decoder_1_out10, decoder_1_out11, decoder_1_out12,
       decoder_1_out13, decoder_1_out14, decoder_1_out15;
  wire [17:0] R0_out_3, R1_out_3, R2_out_3, R3_out_3, R4_out_3, R5_out_3, R6_out_3, R7_out_3, R8_out_3,
       R9_out_3, R10_out_3, R11_out_3, R12_out_3, R13_out_3, R14_out_3, R15_out_3;

  Decoder #(.select(4), .enable("false")) decoder_1 (
    .out0(decoder_1_out0), .out1(decoder_1_out1), .out2(decoder_1_out2), .out3(decoder_1_out3),
    .out4(decoder_1_out4), .out5(decoder_1_out5), .out6(decoder_1_out6), .out7(decoder_1_out7),
    .out8(decoder_1_out8), .out9(decoder_1_out9), .out10(decoder_1_out10), .out11(decoder_1_out11),
    .out12(decoder_1_out12), .out13(decoder_1_out13), .out14(decoder_1_out14), .out15(decoder_1_out15),
    .sel(Dest_Reg));
  and and_1 (and_1_out, decoder_1_out0, write_enable);
  and and_2 (and_2_out, decoder_1_out1, write_enable);
  and and_3 (and_3_out, decoder_1_out2, write_enable);
  and and_4 (and_4_out, decoder_1_out3, write_enable);
  and and_5 (and_5_out, decoder_1_out4, write_enable);
  and and_6 (and_6_out, decoder_1_out5, write_enable);
  and and_7 (and_7_out, decoder_1_out6, write_enable);
  and and_8 (and_8_out, decoder_1_out7, write_enable);
  and and_9 (and_9_out, decoder_1_out8, write_enable);
  and and_10 (and_10_out, decoder_1_out9, write_enable);
  and and_11 (and_11_out, decoder_1_out10, write_enable);
  and and_12 (and_12_out, decoder_1_out11, write_enable);
  and and_13 (and_13_out, decoder_1_out12, write_enable);
  and and_14 (and_14_out, decoder_1_out13, write_enable);
  and and_15 (and_15_out, decoder_1_out14, write_enable);
  and and_16 (and_16_out, decoder_1_out15, write_enable);
  and and_17 (and_17_out, and_1_out, clk);
  and and_18 (and_18_out, and_2_out, clk);
  and and_19 (and_19_out, and_3_out, clk);
  and and_20 (and_20_out, and_4_out, clk);
  and and_21 (and_21_out, and_5_out, clk);
  and and_22 (and_22_out, and_6_out, clk);
  and and_23 (and_23_out, and_7_out, clk);
  and and_24 (and_24_out, and_8_out, clk);
  and and_25 (and_25_out, and_9_out, clk);
  and and_26 (and_26_out, and_10_out, clk);
  and and_27 (and_27_out, and_11_out, clk);
  and and_28 (and_28_out, and_12_out, clk);
  and and_29 (and_29_out, and_13_out, clk);
  and and_30 (and_30_out, and_14_out, clk);
  and and_31 (and_31_out, and_15_out, clk);
  and and_32 (and_32_out, and_16_out, clk);
  _18_bit_Register R0 (.in_1(write_data), .load(and_17_out), .out_3(R0_out_3));
  _18_bit_Register R1 (.in_1(write_data), .load(and_18_out), .out_3(R1_out_3));
  _18_bit_Register R2 (.in_1(write_data), .load(and_19_out), .out_3(R2_out_3));
  _18_bit_Register R3 (.in_1(write_data), .load(and_20_out), .out_3(R3_out_3));
  _18_bit_Register R4 (.in_1(write_data), .load(and_21_out), .out_3(R4_out_3));
  _18_bit_Register R5 (.in_1(write_data), .load(and_22_out), .out_3(R5_out_3));
  _18_bit_Register R6 (.in_1(write_data), .load(and_23_out), .out_3(R6_out_3));
  _18_bit_Register R7 (.in_1(write_data), .load(and_24_out), .out_3(R7_out_3));
  _18_bit_Register R8 (.in_1(write_data), .load(and_25_out), .out_3(R8_out_3));
  _18_bit_Register R9 (.in_1(write_data), .load(and_26_out), .out_3(R9_out_3));
  _18_bit_Register R10 (.in_1(write_data), .load(and_27_out), .out_3(R10_out_3));
  _18_bit_Register R11 (.in_1(write_data), .load(and_28_out), .out_3(R11_out_3));
  _18_bit_Register R12 (.in_1(write_data), .load(and_29_out), .out_3(R12_out_3));
  _18_bit_Register R13 (.in_1(write_data), .load(and_30_out), .out_3(R13_out_3));
  _18_bit_Register R14 (.in_1(write_data), .load(and_31_out), .out_3(R14_out_3));
  _18_bit_Register R15 (.in_1(write_data), .load(and_32_out), .out_3(R15_out_3));
  Multiplexer #(.select(4), .width(18), .enable("false")) multiplexer_1 (
    .in0(R0_out_3), .in1(R1_out_3), .in2(R2_out_3), .in3(R3_out_3), .in4(R4_out_3), .in5(R5_out_3),
    .in6(R6_out_3), .in7(R7_out_3), .in8(R8_out_3), .in9(R9_out_3), .in10(R10_out_3), .in11(R11_out_3),
    .in12(R12_out_3), .in13(R13_out_3), .in14(R14_out_3), .in15(R15_out_3), .out(Src_Data_1), .sel(Src_Reg_1));
  Multiplexer #(.select(4), .width(18), .enable("false")) multiplexer_2 (
    .in0(R0_out_3), .in1(R1_out_3), .in2(R2_out_3), .in3(R3_out_3), .in4(R4_out_3), .in5(R5_out_3),
    .in6(R6_out_3), .in7(R7_out_3), .in8(R8_out_3), .in9(R9_out_3), .in10(R10_out_3), .in11(R11_out_3),
    .in12(R12_out_3), .in13(R13_out_3), .in14(R14_out_3), .in15(R15_out_3), .out(Src_Data_2), .sel(Src_Reg_2));
endmodule

module load_store (
  input  [3:0] \reg ,
  input  Load_Enable,
  input  [9:0] loadedAddress,
  input  ldSig,
  input  stSig,
  input  [17:0] storedAddress
);

  wire [17:0] instruction_unit_1_out_5;

  Register_File register_file_1 (
    .Dest_Reg(\reg ), .write_enable(1'b1), .write_data(instruction_unit_1_out_5), .clk(Load_Enable));  // open: Src_Data_1, Src_Data_2, Src_Reg_1, Src_Reg_2
  instruction_unit instruction_unit_1 (
    .address(loadedAddress), .out_5(instruction_unit_1_out_5), .Load(ldSig), .Store(stSig),
    .dataStored(storedAddress));
endmodule

module andGate (
  input  [17:0] regData1,
  input  [17:0] regData2,
  input  _16th_bit,
  input  [17:0] immValue,
  output [17:0] out_5
);

  wire [17:0] multiplexer_1_out;

  Multiplexer #(.width(18), .enable("false")) multiplexer_1 (
    .in0(regData2), .in1(immValue), .out(multiplexer_1_out), .sel(_16th_bit));
  assign out_5 = regData1 & multiplexer_1_out;  // AND_Gate and_1, 18 bits wide
endmodule

module addGate (
  input  [17:0] regData1,
  input  [17:0] regData2,
  input  _16th_bit,
  input  [17:0] immValue,
  output [17:0] out_5
);

  wire [17:0] multiplexer_1_out;

  Multiplexer #(.width(18), .enable("false")) multiplexer_1 (
    .in0(regData2), .in1(immValue), .out(multiplexer_1_out), .sel(_16th_bit));
  _18_bit_Adder u_18_bit_adder_1 (.out_3(out_5), .Reg_1(multiplexer_1_out), .Reg_2(regData1));
endmodule

module norGate (
  input  [17:0] regData1,
  input  [17:0] regData2,
  output [17:0] out_3
);

  wire [17:0] or_1_out;

  assign or_1_out = regData1 | regData2;  // OR_Gate or_1, 18 bits wide
  assign out_3 = ~or_1_out;  // NOT_Gate not_1, 18 bits wide
endmodule

module nandGate (
  input  [17:0] regData1,
  input  [17:0] regData2,
  output [17:0] out_3
);

  wire [17:0] and_1_out;

  assign and_1_out = regData1 & regData2;  // AND_Gate and_1, 18 bits wide
  assign out_3 = ~and_1_out;  // NOT_Gate not_1, 18 bits wide
endmodule

module Program_Counter_PC (
  input  next,
  input  enableJump,
  input  branch,
  input  clock,
  input  reset,
  input  [9:0] JumpAddress,
  input  [9:0] BranchAddress,
  output [9:0] \output 
);

  wire and_1_out, not_1_out, or_1_out;
  wire [9:0] multiplexer_1_out, result;

  not not_1 (not_1_out, next);
  or or_1 (or_1_out, enableJump, branch);
  and and_1 (and_1_out, not_1_out, or_1_out);
  Counter_part #(.width(10), .max('h3ff)) counter_1 (
    .load(and_1_out), .D(result), .count(next), .Q(\output ), .clk(clock), .clr(reset));  // open: carry
  Multiplexer #(.width(10)) multiplexer_1 (
    .in0(JumpAddress), .in1(BranchAddress), .out(multiplexer_1_out), .sel(branch), .en(enableJump));
  _10_bit_adder u_10_bit_adder_1 (.out_3(result), .PC_2(multiplexer_1_out), .PC(\output ));
endmodule

module _10to1bit_adder (
  input  [9:0] _1,
  input  [9:0] PC,
  output [9:0] out_3
);

  wire half_adder_1_cout, half_adder_3_cout, half_adder_4_cout, half_adder_5_cout, half_adder_6_cout,
       half_adder_7_cout, half_adder_8_cout, half_adder_9_cout, half_adder_10_cout;

  Half_Adder half_adder_1 (.in_1(PC[8]), .in_2(half_adder_4_cout), .Cout(half_adder_1_cout), .S(out_3[8]));
  Half_Adder half_adder_2 (.in_1(PC[9]), .in_2(half_adder_1_cout), .S(out_3[9]));  // open: Cout
  Half_Adder half_adder_3 (.in_1(PC[6]), .in_2(half_adder_6_cout), .Cout(half_adder_3_cout), .S(out_3[6]));
  Half_Adder half_adder_4 (.in_1(PC[7]), .in_2(half_adder_3_cout), .Cout(half_adder_4_cout), .S(out_3[7]));
  Half_Adder half_adder_5 (.in_1(PC[4]), .in_2(half_adder_8_cout), .Cout(half_adder_5_cout), .S(out_3[4]));
  Half_Adder half_adder_6 (.in_1(PC[5]), .in_2(half_adder_5_cout), .Cout(half_adder_6_cout), .S(out_3[5]));
  Half_Adder half_adder_7 (.in_1(PC[2]), .in_2(half_adder_10_cout), .Cout(half_adder_7_cout), .S(out_3[2]));
  Half_Adder half_adder_8 (.in_1(PC[3]), .in_2(half_adder_7_cout), .Cout(half_adder_8_cout), .S(out_3[3]));
  Half_Adder half_adder_9 (.in_1(PC[0]), .in_2(_1[0]), .Cout(half_adder_9_cout), .S(out_3[0]));
  Half_Adder half_adder_10 (.in_1(PC[1]), .in_2(half_adder_9_cout), .Cout(half_adder_10_cout), .S(out_3[1]));
endmodule

module _10_bit_adder (
  input  [9:0] PC,
  input  [9:0] PC_2,
  output [9:0] out_3
);

  wire full_adder_1_cout, full_adder_3_cout, full_adder_4_cout, full_adder_5_cout, full_adder_6_cout,
       full_adder_7_cout, full_adder_8_cout, full_adder_9_cout, half_adder_1_cout;

  Full_Adder full_adder_1 (.i0(PC_2[8]), .i1(PC[8]), .Cin(full_adder_4_cout), .Sum(out_3[8]), .Cout(full_adder_1_cout));
  Full_Adder full_adder_2 (.i0(PC_2[9]), .i1(PC[9]), .Cin(full_adder_1_cout), .Sum(out_3[9]));  // open: Cout
  Full_Adder full_adder_3 (.i0(PC_2[6]), .i1(PC[6]), .Cin(full_adder_6_cout), .Sum(out_3[6]), .Cout(full_adder_3_cout));
  Full_Adder full_adder_4 (.i0(PC_2[7]), .i1(PC[7]), .Cin(full_adder_3_cout), .Sum(out_3[7]), .Cout(full_adder_4_cout));
  Full_Adder full_adder_5 (.i0(PC_2[4]), .i1(PC[4]), .Cin(full_adder_8_cout), .Sum(out_3[4]), .Cout(full_adder_5_cout));
  Full_Adder full_adder_6 (.i0(PC_2[5]), .i1(PC[5]), .Cin(full_adder_5_cout), .Sum(out_3[5]), .Cout(full_adder_6_cout));
  Full_Adder full_adder_7 (.i0(PC_2[2]), .i1(PC[2]), .Cin(full_adder_9_cout), .Sum(out_3[2]), .Cout(full_adder_7_cout));
  Full_Adder full_adder_8 (.i0(PC_2[3]), .i1(PC[3]), .Cin(full_adder_7_cout), .Sum(out_3[3]), .Cout(full_adder_8_cout));
  Half_Adder half_adder_1 (.in_1(PC_2[0]), .in_2(PC[0]), .Cout(half_adder_1_cout), .S(out_3[0]));
  Full_Adder full_adder_9 (.i0(PC_2[1]), .i1(PC[1]), .Cin(half_adder_1_cout), .Sum(out_3[1]), .Cout(full_adder_9_cout));
endmodule

module _1_bit_compare (
  input  in_1,
  input  in_2,
  output Same,
  output GreaterFlag
);

  wire half_adder_1_s, xor_1_out;

  xor xor_1 (xor_1_out, in_1, in_2);
  not not_1 (Same, xor_1_out);
  Half_Adder half_adder_1 (.in_1(in_1), .in_2(in_2), .S(half_adder_1_s));  // open: Cout
  and and_1 (GreaterFlag, half_adder_1_s, in_1);
endmodule

module half_cmp (
  input  a,
  input  b,
  output eq,
  output gt,
  output lt
);

  wire xor_1_out;

  xnor xnor_1 (eq, a, b);
  and and_1 (gt, a, xor_1_out);
  xor xor_1 (xor_1_out, a, b);
  and and_2 (lt, xor_1_out, b);
endmodule

module full_cmp (
  input  a,
  input  b,
  input  gt,
  input  lt,
  input  eq,
  output g,
  output lt_2,
  output eq_2
);

  wire and_1_out, and_2_out, xnor_1_out;

  and and_1 (and_1_out, a, ~b, eq);  // AND_Gate
  and and_2 (and_2_out, ~a, b, eq);  // AND_Gate
  xnor xnor_1 (xnor_1_out, a, b);
  or or_1 (g, and_1_out, gt);
  or or_2 (lt_2, and_2_out, lt);
  and and_3 (eq_2, xnor_1_out, eq);
endmodule

module Control_Unit (
  input  [17:0] _18_bit_input,
  input  [17:0] reg1,
  input  [17:0] reg2,
  output immSig,
  output [3:0] SRC_DEST_OP1,
  output [3:0] SRC1_OP2,
  output [3:0] SRC2,
  output [1:0] ALU_operation,
  output alu,
  output [9:0] ADDREESS10,
  output regWrite,
  output [13:0] ADDRESS_14,
  output [17:0] IMM_ADDRESS6,
  output jumpCond,
  output comparison,
  output [17:0] REG2_data_new,
  output dataMemRead,
  output dataMemWrite,
  output jump
);

  wire ADD, ADDI, AND, and_1_out, and_2_out, and_3_out, and_4_out, and_5_out, ANDI, CMP, cmp_unit_1_eq,
       cmp_unit_1_gt, cmp_unit_1_lt, JA, JAE, JB, JBE, JE, NAND, NOR, or_2_out, or_3_out, or_5_out, or_7_out,
       or_8_out;
  wire [17:0] bit_extender_2_out;

  assign IMM_ADDRESS6 = {{12{_18_bit_input[5]}}, _18_bit_input[5:0]};  // Bit_Extender bit_extender_1
  or or_1 (comparison, JA, JE, JB, JAE, JBE);
  Decoder #(.select(4), .enable("false")) decoder_1 (
    .out0(ADD), .out1(AND), .out2(NAND), .out3(NOR), .out4(ADDI), .out5(ANDI), .out6(dataMemRead),
    .out7(dataMemWrite), .out8(CMP), .out9(jump), .out10(JA), .out11(JE), .out12(JB), .out13(JAE),
    .out14(JBE), .sel(_18_bit_input[17:14]));  // open: out15
  CMP_Unit cmp_unit_1 (.in_1(reg1), .in_2(reg2), .eq(cmp_unit_1_eq), .gt(cmp_unit_1_gt), .lt(cmp_unit_1_lt));
  and and_1 (and_1_out, JE, cmp_unit_1_eq);
  and and_2 (and_2_out, JA, cmp_unit_1_gt);
  or or_2 (or_2_out, cmp_unit_1_gt, cmp_unit_1_eq);
  or or_3 (or_3_out, cmp_unit_1_lt, cmp_unit_1_eq);
  and and_3 (and_3_out, JB, cmp_unit_1_lt);
  assign bit_extender_2_out = {{12{1'b0}}, _18_bit_input[5:0]};  // Bit_Extender bit_extender_2
  or or_4 (regWrite, alu, dataMemRead);
  and and_4 (and_4_out, cmp_unit_1_gt, or_2_out);
  and and_5 (and_5_out, cmp_unit_1_lt, or_3_out);
  or or_5 (or_5_out, immSig, comparison);
  or or_6 (immSig, ANDI, ADDI);
  or or_7 (or_7_out, ADD, ADDI);
  or or_8 (or_8_out, AND, ANDI);
  Multiplexer #(.width(18), .enable("false")) multiplexer_1 (
    .in0(reg2), .in1(bit_extender_2_out), .out(REG2_data_new), .sel(or_5_out));
  Priority_Encoder #(.select(2)) priority_encoder_1 (
    .in0(or_7_out), .in1(or_8_out), .in2(NOR), .in3(NAND), .out(ALU_operation));  // open: gs, en_out, en_in
  or or_9 (jumpCond, and_1_out, and_2_out, and_4_out, and_5_out, and_3_out);
  or or_10 (alu, or_7_out, or_8_out, NOR, NAND);

  assign ADDREESS10 = _18_bit_input[9:0];
  assign ADDRESS_14 = _18_bit_input[13:0];
  assign SRC1_OP2 = _18_bit_input[9:6];
  assign SRC2 = _18_bit_input[5:2];
  assign SRC_DEST_OP1 = _18_bit_input[13:10];

  // Other names for the same wires on the sheet: ADDRESS6[5:0] = _18_bit_input[5:0];
  //   ADDRESS10[9:0] = _18_bit_input[9:0]; ADDRESS14[13:0] = _18_bit_input[13:0]; IMM[5:0] = _18_bit_input[5:0];
  //   OP2[3:0] = _18_bit_input[9:6]; SRC1[3:0] = _18_bit_input[9:6]; ALU_CONTROL = alu; immediate = immSig;
  //   LD = dataMemRead; Opcode[3:0] = _18_bit_input[17:14]; DEST[3:0] = _18_bit_input[13:10];
  //   OP1[3:0] = _18_bit_input[13:10]; SRC[3:0] = _18_bit_input[13:10]; ST = dataMemWrite
endmodule

module Memory_Unit (
  input  [9:0] PC,
  input  counter,
  input  mx_controller,
  output [17:0] out_4
);

  wire program_counter_pc_1_p4;

  // Program_Counter_PC program_counter_pc_1: pin names not known; wires that end beside it: PC, mx_controller, counter, program_counter_pc_1_p4
endmodule

module instruction_unit (
  input  [9:0] address,
  input  [17:0] dataStored,
  input  Store,
  input  Load,
  output [17:0] out_5
);

  RAM #(.addrWidth(10), .dataWidth(18), .bus("separate")) ram_1 (
    .addr(address), .din(dataStored), .data(out_5), .str(Store), .sel(1'b1), .ld(Load), .clr(1'b0));  // open: clk
endmodule

module JPCond (
  input  [17:0] in_1,
  input  [17:0] in_2,
  output JE,
  output JA,
  output JB
);

  CMP_Unit cmp_unit_1 (.in_1(in_1), .in_2(in_2), .eq(JE), .gt(JA), .lt(JB));
endmodule

module Dflipflop (
  input  data,
  input  clk,
  output out_3
);

  wire d_latch_1_out_3, not_1_out;

  D_Latch d_latch_1 (.D(data), .Clock(not_1_out), .out_3(d_latch_1_out_3));  // open: out_4
  not not_1 (not_1_out, clk);
  D_Latch d_latch_2 (.D(d_latch_1_out_3), .Clock(clk), .out_3(out_3));  // open: out_4
endmodule

module Counter (
  input  next,
  input  jump,
  input  clk,
  input  [9:0] data,
  input  reset,
  output [9:0] \output 
);

  wire load_enable, not_1_out, or_1_out;
  wire [9:0] added_value, substracted_value, value_to_load;

  not not_1 (not_1_out, next);
  and and_1 (load_enable, not_1_out, or_1_out);
  or or_1 (or_1_out, jump, data[9]);
  Counter_part #(.width(10), .max('h3ff)) counter_1 (
    .load(load_enable), .D(value_to_load), .count(next), .Q(\output ), .clk(clk), .clr(reset));  // open: carry
  _10_bit_adder u_10_bit_adder_1 (.out_3(added_value), .PC_2(\output ), .PC(data));
  Subtractor #(.width(10)) subtractor_1 (.a(\output ), .b(data), .out(substracted_value));  // open: bin, bout
  assign value_to_load = jump ? added_value : 10'bz;  // Controlled_Buffer controlled_buffer_1
  assign value_to_load = data[9] ? substracted_value : 10'bz;  // Controlled_Buffer controlled_buffer_2

  // Other names for the same wires on the sheet: count = next; input[9:0] = data; substract = data[9]

  // Notes on the sheet:
  //   increment by 1 (count=1, clock ticks)
endmodule

module FSM (
  input  clock,
  input  LD,
  input  ST,
  input  jump,
  input  compraison,
  input  alu,
  output enableWrite,
  output enablePC,
  output nextInst,
  output enableJump
);

  wire alu_pc, alu_wr, branch_pc, controlled_buffer_1_out, controlled_buffer_2_out, controlled_buffer_3_out,
       controlled_buffer_4_out, controlled_buffer_5_out, counter_3_q, decoder_1_out0, decoder_1_out2,
       decoder_2_out0, decoder_2_out2, decoder_3_out0, decoder_3_out1, decoder_4_out1, decoder_4_out2,
       decoder_5_out1, decoder_5_out3, jump_pc, ld_pc, ld_wr, st_pc;
  wire [1:0] counter_1_q, counter_2_q, counter_4_q, counter_5_q;

  assign controlled_buffer_1_out = alu ? clock : 1'bz;  // Controlled_Buffer controlled_buffer_1
  assign controlled_buffer_2_out = LD ? clock : 1'bz;  // Controlled_Buffer controlled_buffer_2
  assign controlled_buffer_3_out = ST ? clock : 1'bz;  // Controlled_Buffer controlled_buffer_3
  Counter_part #(.width(2), .max('h2)) counter_1 (
    .Q(counter_1_q), .clk(controlled_buffer_1_out));  // open: load, D, count, carry, clr
  Counter_part #(.width(2), .max('h2)) counter_2 (
    .Q(counter_2_q), .clk(controlled_buffer_2_out));  // open: load, D, count, carry, clr
  Counter_part #(.width(1), .max('h1)) counter_3 (
    .Q(counter_3_q), .clk(controlled_buffer_3_out));  // open: load, D, count, carry, clr
  Counter_part #(.width(2), .max('h2)) counter_4 (
    .Q(counter_4_q), .clk(controlled_buffer_4_out));  // open: load, D, count, carry, clr
  assign controlled_buffer_4_out = compraison ? clock : 1'bz;  // Controlled_Buffer controlled_buffer_4
  assign controlled_buffer_5_out = jump ? clock : 1'bz;  // Controlled_Buffer controlled_buffer_5
  assign alu_pc = decoder_1_out0 ? 1'b0 : 1'bz;  // Controlled_Buffer controlled_buffer_6
  Decoder #(.select(2), .enable("false")) decoder_1 (
    .out0(decoder_1_out0), .out1(alu_wr), .out2(decoder_1_out2), .sel(counter_1_q));  // open: out3
  Decoder #(.select(2), .enable("false")) decoder_2 (
    .out0(decoder_2_out0), .out1(ld_wr), .out2(decoder_2_out2), .sel(counter_2_q));  // open: out3
  Decoder #(.enable("false")) decoder_3 (.out0(decoder_3_out0), .out1(decoder_3_out1), .sel(counter_3_q));
  Decoder #(.select(2), .enable("false")) decoder_4 (
    .out1(decoder_4_out1), .out2(decoder_4_out2), .sel(counter_4_q));  // open: out0, out3
  Counter_part #(.width(2), .max('h2)) counter_5 (
    .Q(counter_5_q), .clk(controlled_buffer_5_out));  // open: load, D, count, carry, clr
  assign alu_pc = decoder_1_out2 ? 1'b1 : 1'bz;  // Controlled_Buffer controlled_buffer_7
  assign ld_pc = decoder_2_out0 ? 1'b0 : 1'bz;  // Controlled_Buffer controlled_buffer_8
  assign ld_pc = decoder_2_out2 ? 1'b1 : 1'bz;  // Controlled_Buffer controlled_buffer_9
  assign st_pc = decoder_3_out0 ? 1'b0 : 1'bz;  // Controlled_Buffer controlled_buffer_10
  assign st_pc = decoder_3_out1 ? 1'b1 : 1'bz;  // Controlled_Buffer controlled_buffer_11
  assign branch_pc = decoder_4_out1 ? 1'b1 : 1'bz;  // Controlled_Buffer controlled_buffer_12
  assign branch_pc = decoder_4_out2 ? 1'b0 : 1'bz;  // Controlled_Buffer controlled_buffer_13
  assign jump_pc = decoder_5_out1 ? 1'b1 : 1'bz;  // Controlled_Buffer controlled_buffer_14
  Decoder #(.select(2), .enable("false")) decoder_5 (
    .out1(decoder_5_out1), .out3(decoder_5_out3), .sel(counter_5_q));  // open: out0, out2
  assign jump_pc = decoder_5_out3 ? 1'b0 : 1'bz;  // Controlled_Buffer controlled_buffer_15
  or or_1 (enableWrite, alu_wr, ld_wr);
  or or_2 (nextInst, alu_pc, ld_pc, st_pc);
  or or_3 (enableJump, branch_pc, branch_pc, jump_pc, jump_pc);
  or or_4 (enablePC, alu_pc, ld_pc, st_pc, branch_pc, jump_pc);

  // Other names for the same wires on the sheet: comparison = compraison

  // Notes on the sheet:
  //   ALU
  //   LD
  //   ST
  //   Branch
  //   Jump
endmodule
